# Fritzing sketch MCP23017_input (saved by Fritzing 0.9.0b)
breadboards: 1

parts:
  IC1 = IC, DIP package, 28 pins [chip_label=MCP23017]
  R2 = Resistor [tolerance=±5% resistance=1.5k package=THT]
  Bauteil1 = Arduino Uno (Rev3)
  R3 = Resistor [tolerance=±5% resistance=220 package=THT]
  LED1 = LED - 5mm [color="Red (633nm)" package="5 mm [THT]"]
  S1 = Pushbutton [package="[THT]"]
  R4 = Resistor [tolerance=±5% resistance=10k package=THT]
  R1 = Resistor [tolerance=±5% resistance=1.5k package=THT]

nets:
  N1: IC1.pin1, LED1.cathode
  N2: IC1.pin9, R2.Pin_1, Bauteil1.5V, R3.Pin_1, S1.Pin_1, S1.Pin_2, R4.Pin_0, R1.Pin_1
  N3: IC1.pin10, IC1.pin15, IC1.pin16, IC1.pin17, IC1.pin18, Bauteil1.GND, R4.Pin_1
  N4: IC1.pin12, Bauteil1.A5/SCL, R1.Pin_0
  N5: IC1.pin13, R2.Pin_0, Bauteil1.A4/SDA
  N6: IC1.pin21, S1.Pin_3, S1.Pin_4
  N7: R3.Pin_0, LED1.anode
